# Fritzing sketch circuit-diagram (saved by Fritzing 0.9.6b)

parts:
  U1 = NodeMCU V3.0
  S1 = Pushbutton [package="[THT]"]
  Power_plug1 = Power plug
  S2 = H-Bridge with L298N
  A1 = A4988
  M1 = Stepper Motor - Bipolar
  C1 = Electrolytic Capacitor [capacitance=100μF voltage=35V package="0807 [SMD, electrolytic]"]
  LED1 = LED - 5mm [color="Red (633nm)" current=0.030 package="5 mm [THT]"]
  R1 = Resistor [tolerance=±5% resistance=220 package="2010 [SMD]"]
  J1 = Basic Force Sensing Resistor (FSR) [package=THT]

nets:
  N1: U1.D1, A1.ENABLE
  N2: U1.D2, A1.STEP
  N3: U1.D3, A1.DIRECTION
  3V3: U1.3V3, A1.VDD, LED1.anode, J1.pin_1
  N4: U1.GND#6, U1.GND#13, U1.GND#16, S2.GND, A1.GND#13, C1.-, R1.Pin_1
  N5: U1.D5, R1.Pin_0, J1.pin_0
  VIN: U1.Vin, S2.5V
  N6: U1.GND#41, LED1.cathode
  VCC: S1.Pin_3, S1.Pin_4, Power_plug1.VCC, S2.12V, A1.VMOT, C1.+
  N7: Power_plug1.GND, A1.GND#19
  N8: A1.1B, M1.D
  N9: A1.1A, M1.B
  N10: A1.2A, M1.C
  N11: A1.2B, M1.A
  N12: A1.SLEEP, A1.RESET

custom parts:
  NodeMCU V3.0: ESP8266 based NodeMCU
  H-Bridge with L298N: h-bridge
